# Fritzing sketch ultrasonic & LCD (saved by Fritzing 0.9.4)
breadboards: 1

parts:
  Part1 = Arduino Uno (Rev3)
  LCD1 = LCD screen
  U1 = POT [package=pot_mammoth]
  HC-SR04_Sensor_1 = HC-SR04 Ultrasonic Distance Sensor

nets:
  N1: Part1.D9_PWM, HC-SR04_Sensor_1.TRIG
  N2: Part1.D10_PWM/SS, HC-SR04_Sensor_1.ECHO
  N3: Part1.D11_PWM/MOSI, LCD1.E
  N4: Part1.D12/MISO, LCD1.RS
  GND: Part1.GND, LCD1.VSS, LCD1.R/W, LCD1.LED-, U1.E, HC-SR04_Sensor_1.GND
  N5: Part1.D2, LCD1.DB7
  N6: Part1.D3_PWM, LCD1.DB6
  N7: Part1.D4, LCD1.DB5
  N8: Part1.D5_PWM, LCD1.DB4
  5V: Part1.5V, LCD1.VDD, LCD1.LED+, U1.S, HC-SR04_Sensor_1.VCC
  N9: LCD1.V0, U1.A
